# Fritzing sketch Water_Dispenser_Vendo (saved by Fritzing 0.9.3b)
breadboards: 1

parts:
  U1 = ESP32S-HiLetgo [part_number=ESP32S-HiLetgo]
  Part1 = Coin Acceptor - 6-Coin version
  A1 = Bill acceptor TB74-U
  HLK-PM1 = HLK-PM12 [part_number=HLK-PM12]
  M1 = RioRand LM2596
  J1 = Piezo Speaker

nets:
  N1: U1.GPIO25, J1.pin2
  N2: U1.GPIO26, Part1.SIG
  GND: U1.GND, Part1.GND, A1.Pin_1, A1.Pin_2, A1.Pin_3, A1.Pin_4, HLK-PM1.-Vo, M1.Pin_1, M1.Pin_4
  N3: U1.VIN, M1.Pin_3
  N4: U1.GPIO19, A1.Pin_5
  N5: Part1.12V, A1.Pin_6, A1.Pin_10, HLK-PM1.+Vo, M1.Pin_2, J1.pin1

custom parts:
  ESP32S-HiLetgo: HiLetgo ESP-WROOM-32 ESP32 ESP-32S Development Board 2.4GHz Dual-Mode WiFi + Bluetooth Dual Cores Microcontroller The ESP32 integrated with Antenna switches, RF Balun, power amplifiers, low-noise amplifiers, filters, and management modules, and the entire solution occupies the least area of PCB. 2.4 GHz Wi-Fi plus Bluetooth dual-mode chip, with TSMC Ultra-low power consumption 40nm technology,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
  Coin Acceptor - 6-Coin version: 12V coin acceptor that can handle up to 6 different denominations. Output is either pulse width, serial, or single pin per coin value.
  Bill acceptor TB74-U: The TB-Series is the latest generation of banknote reader designed exclusively by TOPVME with the highest safety and acceptance rate have over 96%.
